// Logisim project Project.circ as structural Verilog: 5 circuits, main circuit CPU
module CPU (
  input  in_1,
  input  Clear_Memory,
  output [19:0] out_3
);

  wire alu_1_zf, and_1_out, beq, clock_1_out, control_unit_1_lw, control_unit_1_sw, or_1_out, or_2_out,
       R_Type;
  wire [3:0] acu_1_out_4, multiplexer_2_out;
  wire [19:0] adder_1_out, alu_1_output, bit_extender_1_out, multiplexer_1_out, multiplexer_3_out,
       multiplexer_4_out, PC_q, ram_1_data, register_file_1_out_reg1, register_file_1_out_reg2, rom_1_data;

  Clock clock_1 (.out(clock_1_out));
  Adder #(.width(20)) adder_1 (.a(PC_q), .b(multiplexer_1_out), .out(adder_1_out));  // open: cin, cout
  Register #(.width(20)) PC (.D(adder_1_out), .Q(PC_q), .clk(clock_1_out), .clr(in_1));  // open: en
  ROM #(.addrWidth(20), .dataWidth(20)) rom_1 (.addr(PC_q), .data(rom_1_data));  // open: sel
  Multiplexer #(.width(20), .enable("false")) multiplexer_1 (
    .in0(20'h1), .in1(bit_extender_1_out), .out(multiplexer_1_out), .sel(and_1_out));
  and and_1 (and_1_out, alu_1_zf, beq);
  Multiplexer #(.width(4), .enable("false")) multiplexer_2 (
    .in0(rom_1_data[11:8]), .in1(rom_1_data[7:4]), .out(multiplexer_2_out), .sel(R_Type));
  assign bit_extender_1_out = {{12{rom_1_data[7]}}, rom_1_data[7:0]};  // Bit_Extender bit_extender_1
  Control_Unit control_unit_1 (
    .Op_code(rom_1_data[19:16]), .beq(beq), .lw(control_unit_1_lw), .sw(control_unit_1_sw), .R_Type(R_Type));
  ACU acu_1 (.func(rom_1_data[3:0]), .beq(beq), .R_Type(R_Type), .out_4(acu_1_out_4));
  or or_1 (or_1_out, control_unit_1_lw, R_Type);
  Register_File register_file_1 (
    .R_W(or_1_out), .Data(multiplexer_4_out), .Reset(in_1), .Out_Reg1(register_file_1_out_reg1),
    .Out_Reg2(register_file_1_out_reg2), .Clock(clock_1_out), .Reg1(rom_1_data[15:12]),
    .Dest(multiplexer_2_out), .test(out_3), .Reg2(rom_1_data[11:8]));
  Multiplexer #(.width(20), .enable("false")) multiplexer_3 (
    .in0(bit_extender_1_out), .in1(register_file_1_out_reg2), .out(multiplexer_3_out), .sel(or_2_out));
  or or_2 (or_2_out, beq, R_Type);
  Multiplexer #(.width(20), .enable("false")) multiplexer_4 (
    .in0(alu_1_output), .in1(ram_1_data), .out(multiplexer_4_out), .sel(control_unit_1_lw));
  ALU alu_1 (
    .Input_1(register_file_1_out_reg1), .Input_2(multiplexer_3_out), .Output(alu_1_output),
    .Function(acu_1_out_4), .ZF(alu_1_zf));
  RAM #(.addrWidth(20), .dataWidth(20), .bus("separate")) ram_1 (
    .addr(alu_1_output), .din(register_file_1_out_reg2), .data(ram_1_data), .str(control_unit_1_sw),
    .clk(clock_1_out), .ld(control_unit_1_lw), .clr(Clear_Memory));  // open: sel

  // Notes on the sheet:
  //   contents of rom_1 (hex, n*v repeats v):
  //   0 20101 20202 1237
  //   ACU
  //   Reg 3
endmodule

module ALU (
  input  [3:0] Function,
  input  [19:0] Input_1,
  input  [19:0] Input_2,
  output [19:0] Output,
  output ZF
);

  wire [19:0] adder_1_out, and_1_out, divider_1_out, divider_1_rem, multiplier_1_out, or_1_out,
       subtractor_1_out, xor_1_out;

  assign and_1_out = Input_1 & Input_2;  // AND_Gate and_1, 20 bits wide
  assign or_1_out = Input_1 | Input_2;  // OR_Gate or_1, 20 bits wide
  assign xor_1_out = Input_1 ^ Input_2;  // XOR_Gate xor_1, 20 bits wide
  Adder #(.width(20)) adder_1 (.a(Input_1), .b(Input_2), .out(adder_1_out));  // open: cin, cout
  Subtractor #(.width(20)) subtractor_1 (.a(Input_1), .b(Input_2), .out(subtractor_1_out));  // open: bin, bout
  Multiplier #(.width(20)) multiplier_1 (.a(Input_1), .b(Input_2), .out(multiplier_1_out));  // open: cin, cout
  Divider #(.width(20)) divider_1 (.a(Input_1), .b(Input_2), .out(divider_1_out), .rem(divider_1_rem));  // open: upper
  Multiplexer #(.select(4), .width(20), .enable("false")) multiplexer_1 (
    .in0(and_1_out), .in1(or_1_out), .in2(xor_1_out), .in3(adder_1_out), .in4(subtractor_1_out),
    .in5(multiplier_1_out), .in6(divider_1_out), .in7(divider_1_rem), .in8({20{1'b0}}), .in9({20{1'b0}}),
    .in10({20{1'b0}}), .in11({20{1'b0}}), .in12({20{1'b0}}), .in13({20{1'b0}}), .in14({20{1'b0}}),
    .in15({20{1'b0}}), .out(Output), .sel(Function));
  nor nor_1 (ZF, Output[19], Output[18], Output[17], Output[16], Output[15], Output[14], Output[13], Output[12], Output[11], Output[10], Output[9], Output[8], Output[7], Output[6], Output[5], Output[4], Output[3], Output[2], Output[1], Output[0]);
endmodule

module Register_File (
  input  R_W,
  input  [3:0] Dest,
  input  [19:0] Data,
  input  Clock,
  input  [3:0] Reg1,
  input  Reset,
  input  [3:0] Reg2,
  output [19:0] Out_Reg1,
  output [19:0] test,
  output [19:0] Out_Reg2
);

  wire and_1_out, and_2_out, and_3_out, and_4_out, and_5_out, and_6_out, and_7_out, and_8_out,
       demultiplexer_1_out0, demultiplexer_1_out1, demultiplexer_1_out2, demultiplexer_1_out3,
       demultiplexer_1_out4, demultiplexer_1_out5, demultiplexer_1_out6, demultiplexer_1_out7;
  wire [19:0] R0_q, R1_q, R2_q, R4_q, R5_q, R6_q, R7_q, register_1_q;

  Register #(.width(20)) register_1 (.D(Data), .Q(register_1_q), .clk(Clock), .clr(Reset));  // open: en
  Demultiplexer #(.select(4), .enable("false")) demultiplexer_1 (
    .out0(demultiplexer_1_out0), .out1(demultiplexer_1_out1), .out2(demultiplexer_1_out2),
    .out3(demultiplexer_1_out3), .out4(demultiplexer_1_out4), .out5(demultiplexer_1_out5),
    .out6(demultiplexer_1_out6), .out7(demultiplexer_1_out7), .in(1'b1), .sel(Dest));  // open: out8, out9, out10, out11, out12, out13, out14, out15
  and and_1 (and_1_out, R_W, demultiplexer_1_out0);
  and and_2 (and_2_out, demultiplexer_1_out1, R_W);
  and and_3 (and_3_out, demultiplexer_1_out2, R_W);
  and and_4 (and_4_out, demultiplexer_1_out3, R_W);
  and and_5 (and_5_out, demultiplexer_1_out4, R_W);
  and and_6 (and_6_out, demultiplexer_1_out5, R_W);
  and and_7 (and_7_out, demultiplexer_1_out6, R_W);
  and and_8 (and_8_out, demultiplexer_1_out7, R_W);
  Register #(.width(20), .trigger("high")) R0 (.D(register_1_q), .Q(R0_q), .clk(and_1_out), .clr(Reset));  // open: en
  Register #(.width(20), .trigger("high")) R1 (.D(register_1_q), .Q(R1_q), .clk(and_2_out), .clr(Reset));  // open: en
  Register #(.width(20), .trigger("high")) R2 (.D(register_1_q), .Q(R2_q), .clk(and_3_out), .clr(Reset));  // open: en
  Register #(.width(20), .trigger("high")) R3 (.D(register_1_q), .Q(test), .clk(and_4_out), .clr(Reset));  // open: en
  Register #(.width(20), .trigger("high")) R4 (.D(register_1_q), .Q(R4_q), .clk(and_5_out), .clr(Reset));  // open: en
  Register #(.width(20), .trigger("high")) R5 (.D(register_1_q), .Q(R5_q), .clk(and_6_out), .clr(Reset));  // open: en
  Register #(.width(20), .trigger("high")) R6 (.D(register_1_q), .Q(R6_q), .clk(and_7_out), .clr(Reset));  // open: en
  Register #(.width(20), .trigger("high")) R7 (.D(register_1_q), .Q(R7_q), .clk(and_8_out), .clr(Reset));  // open: en
  Multiplexer #(.select(4), .width(20), .enable("false")) multiplexer_1 (
    .in0(R0_q), .in1(R1_q), .in2(R2_q), .in3(test), .in4(R4_q), .in5(R5_q), .in6(R6_q), .in7(R7_q),
    .out(Out_Reg1), .sel(Reg1));  // open: in8, in9, in10, in11, in12, in13, in14, in15
  Multiplexer #(.select(4), .width(20), .enable("false")) multiplexer_2 (
    .in0(R0_q), .in1(R1_q), .in2(R2_q), .in3(test), .in4(R4_q), .in5(R5_q), .in6(R6_q), .in7(R7_q),
    .out(Out_Reg2), .sel(Reg2));  // open: in8, in9, in10, in11, in12, in13, in14, in15
endmodule

module Control_Unit (
  input  [3:0] Op_code,
  output beq,
  output lw,
  output sw,
  output R_Type
);

  wire not_1_out, not_2_out, not_3_out, not_4_out, not_5_out, not_6_out, not_7_out, not_8_out;

  not not_1 (not_1_out, Op_code[3]);
  not not_2 (not_2_out, Op_code[3]);
  not not_3 (not_3_out, Op_code[0]);
  not not_4 (not_4_out, Op_code[2]);
  not not_5 (not_5_out, Op_code[3]);
  not not_6 (not_6_out, Op_code[1]);
  not not_7 (not_7_out, Op_code[2]);
  not not_8 (not_8_out, Op_code[3]);
  and and_1 (beq, Op_code[0], Op_code[1], not_1_out, not_2_out);
  and and_2 (lw, not_3_out, Op_code[1], not_4_out, not_5_out);
  and and_3 (sw, Op_code[0], not_6_out, not_7_out, not_8_out);
  nor nor_1 (R_Type, Op_code[0], Op_code[1], Op_code[2], Op_code[3]);
endmodule

module ACU (
  input  [3:0] func,
  input  beq,
  input  R_Type,
  output [3:0] out_4
);

  wire or_1_out;
  wire [3:0] multiplexer_1_out;

  Multiplexer #(.width(4), .enable("false")) multiplexer_1 (
    .in0(func), .in1(4'b0010), .out(multiplexer_1_out), .sel(beq));
  Multiplexer #(.width(4), .enable("false")) multiplexer_2 (
    .in0(4'b0011), .in1(multiplexer_1_out), .out(out_4), .sel(or_1_out));
  or or_1 (or_1_out, beq, R_Type);
endmodule
